// Logisim project CPU Core.circ as structural Verilog: 2 circuits, main circuit Core
module Core (
  output [31:0] Loaded_data_not_saved_to_RegFile,
  output [31:0] fetched_inst
);

  wire clk_out, Controller_load_en, Controller_reg_en, Controller_store_en;
  wire [2:0] Decoder_func3;
  wire [4:0] Decoder_id_out, Decoder_rd, Decoder_rs1, Decoder_rs2;
  wire [6:0] Decoder_func7;
  wire [31:0] ALU_out, Decoder_imm, demultiplexer_1_out0, demultiplexer_1_out1, ram_1_data, RegFile_rs1_data,
       RegFile_rs2_data, rs2_imm_Generator_out;

  Clock clk (.out(clk_out));
  Fetch Fetch (.inst_out(fetched_inst), .clk(clk_out));  // open: reset
  Decoder Decoder (
    .inst_in(fetched_inst), .rd(Decoder_rd), .func3(Decoder_func3), .rs1(Decoder_rs1), .rs2(Decoder_rs2),
    .func7(Decoder_func7), .imm(Decoder_imm), .ID_out(Decoder_id_out));  // open: opcode
  assign Loaded_data_not_saved_to_RegFile = demultiplexer_1_out1 | demultiplexer_1_out0;  // OR_Gate or_1, 32 bits wide
  Demultiplexer #(.width(32), .enable("false")) demultiplexer_1 (
    .out0(demultiplexer_1_out0), .out1(demultiplexer_1_out1), .in(ram_1_data), .sel(Controller_reg_en));
  Register_File RegFile (
    .write_in(demultiplexer_1_out1), .clk(clk_out), .rs1_data(RegFile_rs1_data), .rs1_addr(Decoder_rs1),
    .rs2_data(RegFile_rs2_data), .rs2_addr(Decoder_rs2), .write_addr(Decoder_rd));
  rs2_imm_Generator rs2_imm_Generator (
    .rs2_data(RegFile_rs2_data), .imm(Decoder_imm), .ID(Decoder_id_out), .out(rs2_imm_Generator_out));
  ALU ALU (
    .rs1_data(RegFile_rs1_data), .rs2_imm_data(rs2_imm_Generator_out), .out(ALU_out), .func3(Decoder_func3),
    .func7(Decoder_func7), .ID(Decoder_id_out));
  Controller Controller (
    .ID(Decoder_id_out), .store_en(Controller_store_en), .load_en(Controller_load_en),
    .reg_en(Controller_reg_en));
  RAM #(.addrWidth(24), .dataWidth(32), .bus("separate")) ram_1 (
    .addr(ALU_out[23:0]), .din(rs2_imm_Generator_out), .data(ram_1_data), .str(Controller_store_en),
    .sel(1'b1), .clk(clk_out), .ld(Controller_load_en));  // open: clr
endmodule

module rs2_imm_Generator (
  input  [31:0] rs2_data,
  input  [31:0] imm,
  input  [4:0] ID,
  output [31:0] out
);

  Multiplexer #(.select(2), .width(32), .enable("false")) multiplexer_1 (
    .in1(imm), .in2(rs2_data), .in3(rs2_data), .out(out), .sel(ID[3:2]));  // open: in0
endmodule
