// Logisim project Controller.circ as structural Verilog: 1 circuit, main circuit Controller
module Controller (
  input  [4:0] ID,
  output store_en,
  output load_en,
  output jal
);

  Comparator #(.width(3), .mode("unsigned")) comparator_1 (.a(3'b010), .b(ID[4:2]), .eq(store_en));  // open: gt, lt
  Comparator #(.width(5), .mode("unsigned")) comparator_2 (.a({5{1'b0}}), .b(ID), .eq(load_en));  // open: gt, lt
  Comparator #(.width(5), .mode("unsigned")) comparator_3 (.a(ID), .b(5'b11011), .eq(jal));  // open: gt, lt
endmodule
