// Logisim project Fetch.circ as structural Verilog: 1 circuit, main circuit Fetch
module Fetch (
  input  [31:0] nextPC,
  input  nPC_en,
  input  clk,
  input  reset,
  output [23:0] inst_out,
  output [31:0] PC_out
);

  wire [31:0] adder_1_out, multiplexer_1_out;

  Multiplexer #(.width(32), .enable("false")) multiplexer_1 (
    .in0(adder_1_out), .in1(nextPC), .out(multiplexer_1_out), .sel(nPC_en));
  Register #(.width(32)) PC (
    .D(multiplexer_1_out), .en(1'b1), .Q({PC_out[31:26], inst_out, PC_out[1:0]}), .clk(clk), .clr(reset));
  Adder #(.width(32)) adder_1 (
    .a(32'h4), .b({PC_out[31:26], inst_out, PC_out[1:0]}), .out(adder_1_out));  // open: cin, cout

  assign PC_out[25:2] = inst_out;
endmodule
